// Logisim project 2.4.1.circ as structural Verilog: 1 circuit, main circuit main
module main (
  input  in_1,
  input  SW1,
  input  SW2
);

  wire n7404_1_p3, n7408_1_p4;

  // _7404 7404_1: pin names not known; wires that end beside it: 1'b1, in_1, n7404_1_p3, 1'b0
  // _7408 7408_1: pin names not known; wires that end beside it: 1'b1, SW1, SW2, n7408_1_p4, 1'b0
  LED led_1 (.in(n7404_1_p3));
  LED led_2 (.in(n7408_1_p4));

  // Notes on the sheet:
  //   SW1
  //   U1
  //   U1
  //   LED0
  //   LED0
  //   5V - U1:14
  //   GND - U1:7
  //   SW1 - U1:1
  //   U1:2 - LED0
  //   5V - U1:14
  //   GND - U1:7
  //   SW1 - U1:1
  //   SW2 - U1:2
  //   U1:3 - LED0
endmodule
