// Logisim project 2.4.2a.circ as structural Verilog: 1 circuit, main circuit main
module main (
  input  SW1,
  input  SW2,
  input  SW3
);

  wire n7404_1_p3, n7408_1_p4, n7432_1_p4;

  // _7408 7408_1: pin names not known; wires that end beside it: 1'b1, SW1, SW2, n7408_1_p4, 1'b0
  // _7404 7404_1: pin names not known; wires that end beside it: 1'b1, SW3, n7404_1_p3, 1'b0
  // _7432 7432_1: pin names not known; wires that end beside it: 1'b1, n7408_1_p4, n7404_1_p3, n7432_1_p4, 1'b0
  LED led_1 (.in(n7432_1_p4));

  // Notes on the sheet:
  //   U1
  //   U3
  //   U2
  //   LED0
  //   5V - U1: 14
  //   GND - U1: 7
  //   SW1 - U1: 1
  //   SW2 - U1: 2
  //   U1: 3 - U2: 1
  //   5V - U3: 14
  //   GND - U3: 7
  //   SW3 - U3: 1
  //   U3: 2 - U2: 2
  //   5V - U2: 14
  //   GND - U2: 7
  //   U2: 3 - LED0
endmodule
