// Logisim project 2.4.3a.circ as structural Verilog: 1 circuit, main circuit main
module main (
  input  in_1,
  input  in_2,
  input  in_3
);

  wire n7404_1_pin2, n7404_1_pin8, n7404_1_pin10, n7408_1_pin3, n7408_1_pin6, n7408_1_pin8, n7408_1_pin11,
       n7432_1_p4;

  _7404 u_7404_1 (
    .pin1(in_2), .pin2(n7404_1_pin2), .pin11(in_3), .pin10(n7404_1_pin10), .pin9(in_1), .pin8(n7404_1_pin8));  // open: pin3, pin4, pin5, pin6, pin13, pin12
  _7408 u_7408_1 (
    .pin1(in_1), .pin2(n7404_1_pin2), .pin3(n7408_1_pin3), .pin4(n7408_1_pin3), .pin5(in_3),
    .pin6(n7408_1_pin6), .pin13(n7404_1_pin8), .pin12(in_2), .pin11(n7408_1_pin11), .pin10(n7408_1_pin11),
    .pin9(n7404_1_pin10), .pin8(n7408_1_pin8));
  // _7432 7432_1: pin names not known; wires that end beside it: 1'b1, n7408_1_pin6, n7408_1_pin8, n7432_1_p4, 1'b0
  LED led_1 (.in(n7432_1_p4));

  // Notes on the sheet:
  //   M
  //   N
  //   P
  //    _
  //   _
  //   M.N.P + M.N.P
  //   _
  //   LED0
endmodule
