// Logisim project 2.4.3b.circ as structural Verilog: 1 circuit, main circuit main
module main (
  input  in_1,
  input  in_2
);

  wire n7432_1_p4;

  // _7432 7432_1: pin names not known; wires that end beside it: 1'b1, in_1, in_2, n7432_1_p4, 1'b0
  LED led_1 (.in(n7432_1_p4));

  // Notes on the sheet:
  //   A
  //   B
  //   W = A + B
  //   LED0
endmodule
